// Digital circuit Prueba1.dig as structural Verilog
module Prueba1 (
  input  x,
  input  y,
  input  s,
  output out
);

  wire s_t, x_s, y_s;

  _7404 _7404_1 (
    .pin1(s), .pin2(s_t), .pin3(1'b0), .pin5(1'b0), .pin7(1'b0), .pin8(1'b0), .pin9(x_s), .pin10(x),
    .pin11(s_t), .pin12(y_s), .pin13(y), .pin14(s));  // open: pin4, pin6
  _7408 _7408_1 (
    .pin1(s), .pin2(y), .pin3(y_s), .pin4(s_t), .pin5(x), .pin6(x_s), .pin7(1'b0), .pin8(1'b0), .pin10(1'b0),
    .pin11(1'b0), .pin12(out), .pin13(x_s), .pin14(y_s));  // open: pin9
  _7432 _7432_1 (
    .pin1(y_s), .pin2(x_s), .pin3(out), .pin4(1'b0), .pin5(1'b0), .pin7(1'b0), .pin9(1'b1), .pin10(1'b1),
    .pin12(1'b1), .pin13(1'b1), .pin14(1'b1));  // open: pin6, pin8, pin11

  // Notes on the sheet:
  //   x: default 1
  //   y: default 1
  //   s: default 1
endmodule

/* Test case:
x y s out
0 0 0 0
0 0 1 0
0 1 0 0
0 1 1 1
1 0 0 1
1 0 1 0
1 1 0 1
1 1 1 1
*/
